# Fritzing sketch temp_humidity (saved by Fritzing 0.9.3b)
breadboards: 1

parts:
  Amica_NodeMCU_DevKit_1_1 = Amica NodeMCU DevKit 1.0
  DHT1 = DHT22 Humidity and Temperature Sensor
  Squix1 = OLED 0.96" 128x64 I2C SSD1306

nets:
  VDD: Amica_NodeMCU_DevKit_1_1.pin1, Amica_NodeMCU_DevKit_1_1.pin_10, Amica_NodeMCU_DevKit_1_1.pin_26, DHT1.VDD, Squix1.VCC
  GND: Amica_NodeMCU_DevKit_1_1.pin2, Amica_NodeMCU_DevKit_1_1.pin_9, Amica_NodeMCU_DevKit_1_1.pin_25, Amica_NodeMCU_DevKit_1_1.pin_29, DHT1.GND, Squix1.GND
  N1: Amica_NodeMCU_DevKit_1_1.pin8, DHT1.DATA
  N2: Amica_NodeMCU_DevKit_1_1.pin_13, Squix1.SCA
  N3: Amica_NodeMCU_DevKit_1_1.pin_14, Squix1.SCL

custom parts:
  Amica NodeMCU DevKit 1.0: Amica NodeMCU DEVKIT 1.0 Development Kit based on ESP8266 ESP-12E, integating GPIO, PWM, IIC, 1-Wire and ADC all in one board.
